# Fritzing sketch biggreenbutton (saved by Fritzing 0.9.2b)
breadboards: 1

parts:
  Raspberry_Pi1 = Raspberry Pi B+
  Power_plug1 = Power plug
  S1 = Round Pushbutton
  GPS1 = Adafruit Ultimate GPS Breakout
  USBTTL1 = USB TTL Serial Cable
  LED1 = smd LED [color="Red (633nm)" package="0603 [SMD]"]
  K3 = Relay [part_number=FRS1B-S package=THT]
  Part1 = Thermal Printer

nets:
  N1: Raspberry_Pi1.GND, S1.leg0, LED1.cathode, K3.COIL2, Part1.GND#2
  N2: Raspberry_Pi1.GPIO16, K3.COIL1
  N3: Raspberry_Pi1.GPIO12, S1.leg1
  N4: Raspberry_Pi1.GPIO14, Part1.RXD
  N5: Power_plug1.VCC, K3.C2
  N6: Power_plug1.GND, Part1.GND#0
  N7: GPS1.FIX, LED1.anode
  N8: GPS1.TX, USBTTL1.RX
  N9: GPS1.RX, USBTTL1.TX
  GND: GPS1.GND, USBTTL1.GND
  VIN: GPS1.VIN, USBTTL1.5V
  N10: K3.A, Part1.VH
